# Fritzing sketch Estación de Temperatura (saved by Fritzing 0.9.10b)
breadboards: 3

parts:
  Componente1 = Arduino Pro Mini v13
  LCD1 = LCD screen
  LCM1602_IIC1 = generic_ic_dip_22_300mil.fzp [part_number="LCM1602 IIC" chip_label="LCM1602 IIC"]
  Power_plug1 = Power plug
  LED1 = RGB LED (com. cathode, rgb) [package="5 mm [THT]"]
  R1 = Resistor [tolerance=±5% power=0.25 resistance=330 package=THT]
  U1 = Voltage Regulator - 5V [package="TO220 [THT]"]
  C2 = Capacitor [package=cap-pth-small2]
  C3 = Capacitor [package=cap-pth-small2]
  D1 = Rectifier Diode [part_number=1N4001 package="300 mil [THT]"]
  D2 = Rectifier Diode [part_number=1N4001 package="300 mil [THT]"]
  U2 = Voltage Regulator - 5V [package="TO220 [THT]"]
  C4 = Capacitor [package=cap-pth-small2]
  C5 = Capacitor [package=cap-pth-small2]
  D3 = Rectifier Diode [part_number=1N4001 package="300 mil [THT]"]
  D4 = Rectifier Diode [part_number=1N4001 package="300 mil [THT]"]
  Mod1 = KY-015 Temperature & Humidity Sensor Module [package="Breakout board"]

nets:
  GND: Componente1.GND, LCD1.VSS, LCM1602_IIC1.connector0, LCM1602_IIC1.connector16, Power_plug1.GND, R1.Pin_0, U1.GND, C2.1, C3.2, D2.anode, U2.GND, C4.2, C5.1, D4.anode, Mod1.-
  N1: Componente1.RAW, D2.cathode, Mod1.Vin
  N2: Componente1.D7, LED1.blue_anode
  N3: Componente1.D6_PWM, LED1.green_anode
  N4: Componente1.D5_PWM, LED1.red_anode
  N5: Componente1.D4, Mod1.S
  N6: LCD1.VDD, LCM1602_IIC1.connector1
  N7: LCD1.V0, LCM1602_IIC1.connector2
  N8: LCD1.RS, LCM1602_IIC1.connector3
  N9: LCD1.R/W, LCM1602_IIC1.connector4
  N10: LCD1.E, LCM1602_IIC1.connector5
  N11: LCD1.DB0, LCM1602_IIC1.connector6
  N12: LCD1.DB1, LCM1602_IIC1.connector7
  N13: LCD1.DB2, LCM1602_IIC1.connector8
  N14: LCD1.DB3, LCM1602_IIC1.connector9
  N15: LCD1.DB4, LCM1602_IIC1.connector10
  N16: LCD1.DB5, LCM1602_IIC1.connector11
  N17: LCD1.DB6, LCM1602_IIC1.connector12
  N18: LCD1.DB7, LCM1602_IIC1.connector13
  N19: LCD1.LED+, LCM1602_IIC1.connector14
  N20: LCD1.LED-, LCM1602_IIC1.connector15
  N21: LCM1602_IIC1.connector17, D4.cathode
  N22: LCM1602_IIC1.connector20, LCM1602_IIC1.connector21
  N23: Power_plug1.VCC, U1.input_voltage, C3.1, D1.cathode, U2.input_voltage, C4.1, D3.cathode
  N24: LED1.common_cathode, R1.Pin_1
  N25: U1.output_voltage, C2.2, D1.anode
  N26: U2.output_voltage, C5.2, D3.anode

notes:
  SDA = A4
  SCL = A5
  Regulador 7805= 5v

custom parts:
  KY-015 Temperature & Humidity Sensor Module: KY-015 temperature and humidity sensor module, provides a low-latency serial interface to measure humidity and temperature.
